# Fritzing sketch ProjektBrutKasten (saved by Fritzing 0.9.2b)
circuit board: 12.4cm x 6.7cm
breadboards: 1

parts:
  U1 = attiny85 [package=dip]
  U2 = Voltage Regulator - 5V [package="TO220 [THT]"]
  VCC1 = Battery block 9V
  LED1 = RGB LED (shift register, rgb) [package="8 mm [THT]"]
  LED2 = RGB LED (shift register, rgb) [package="8 mm [THT]"]
  LED3 = RGB LED (shift register, rgb) [package="8 mm [THT]"]
  LED4 = RGB LED (shift register, rgb) [package="8 mm [THT]"]
  LED5 = RGB LED (shift register, rgb) [package="8 mm [THT]"]
  LED6 = RGB LED (shift register, rgb) [package="8 mm [THT]"]

nets:
  GND: U1.Pin_4, U2.GND, VCC1.-, LED1.GND, LED2.GND, LED3.GND, LED4.GND, LED5.GND, LED6.GND
  N1: U1.Pin_6, LED1.DIN
  VDD: U1.Pin_8, U2.output_voltage, LED1.VDD, LED2.VDD, LED3.VDD, LED4.VDD, LED5.VDD, LED6.VDD
  N2: U2.input_voltage, VCC1.+
  N3: LED1.DOUT, LED2.DIN
  N4: LED2.DOUT, LED3.DIN
  N5: LED3.DOUT, LED4.DIN
  N6: LED4.DOUT, LED5.DIN
  N7: LED5.DOUT, LED6.DIN

custom parts:
  RGB LED (shift register, rgb): A 5 or 8 mm RGB LED
