# Fritzing sketch ProjektBrutKasten_PoC (saved by Fritzing 0.9.2b)
breadboards: 1

parts:
  Bauteil1 = Arduino Uno (Rev3)
  LED1 = RGB LED (shift register, rgb) [package="8 mm [THT]"]
  LED2 = RGB LED (shift register, rgb) [package="8 mm [THT]"]

nets:
  N1: Bauteil1.D5_PWM, LED2.DIN
  VDD: Bauteil1.5V, LED1.VDD, LED2.VDD
  GND: Bauteil1.GND, LED1.GND, LED2.GND
  N2: LED1.DIN, LED2.DOUT

custom parts:
  RGB LED (shift register, rgb): A 5 or 8 mm RGB LED
